# Fritzing sketch plug_jack_test (saved by Fritzing 0.9.3b)

parts:
  J1 = Power Plug
  J2 = Power Jack [package=power_jack_slot]
  J3 = female pin header, 2 pins [form="♀ (female)"]
  J4 = female pin header, 2 pins [form="♀ (female)"]

nets:
  GND: J1.GND, J1.tip_GND, J2.GND, J2.tip_GND, J3.pin1, J4.pin2
  N1: J1.PWR, J1.tip_PWR, J2.PWR, J2.tip_PWR, J3.pin2, J4.pin1

custom parts:
  Power Plug: Power Jack This is the standard 5.5mm barrel plug for power. This part has bendable leads (i.e. wires in the real world) to connect to wall warts or the breadboard in the standard wire end, and hidden connectors on the tip end that will connect when "plugged in" (overlapped with the jack so it appears "plugged in" in breadboard) to the modified coax jack part. Internal busses connect the two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
  Power Jack: Power Jack This is the standard 5.5mm barrel jack for power. Ths one is modified to mate with the barrel plug part and allow the two to "connect" so batteries and wall warts can be "connected" in breadboard and will go through to schematic.
